// Logisim project register.circ as structural Verilog: 1 circuit, main circuit main
module main (
  input  [4:0] Write__Register,
  input  [4:0] Read__Register_1,
  input  [4:0] Read__Register_2,
  input  [31:0] Write_Data,
  input  RegWEn,
  input  clk,
  output [31:0] Read_Data_1,
  output [31:0] Read_Data_2
);

  wire and_1_out, and_2_out, and_3_out, and_4_out, and_5_out, and_6_out, and_7_out, and_8_out, and_9_out,
       decoder_1_out0, decoder_1_out1, decoder_1_out2, decoder_1_out5, decoder_1_out6, decoder_1_out7,
       decoder_1_out8, decoder_1_out9, decoder_1_out10;
  wire [31:0] x0_q, x1_q, x2_q, x5_q, x6_q, x7_q, x8_q, x9_q, x10_q;

  Decoder #(.select(4), .enable("false")) decoder_1 (
    .out0(decoder_1_out0), .out1(decoder_1_out1), .out2(decoder_1_out2), .out5(decoder_1_out5),
    .out6(decoder_1_out6), .out7(decoder_1_out7), .out8(decoder_1_out8), .out9(decoder_1_out9),
    .out10(decoder_1_out10), .sel(Write__Register[3:0]));  // open: out3, out4, out11, out12, out13, out14, out15
  and and_1 (and_1_out, RegWEn, decoder_1_out0);
  and and_2 (and_2_out, RegWEn, decoder_1_out1);
  and and_3 (and_3_out, RegWEn, decoder_1_out10);
  and and_4 (and_4_out, RegWEn, decoder_1_out2);
  and and_5 (and_5_out, RegWEn, decoder_1_out5);
  and and_6 (and_6_out, RegWEn, decoder_1_out6);
  and and_7 (and_7_out, RegWEn, decoder_1_out7);
  and and_8 (and_8_out, RegWEn, decoder_1_out8);
  and and_9 (and_9_out, RegWEn, decoder_1_out9);
  Register #(.width(32)) x0 (.D({32{1'b0}}), .en(and_1_out), .Q(x0_q), .clk(clk));  // open: clr
  Register #(.width(32)) x1 (.D(Write_Data), .en(and_2_out), .Q(x1_q), .clk(clk));  // open: clr
  Register #(.width(32)) x2 (.D(Write_Data), .en(and_4_out), .Q(x2_q), .clk(clk));  // open: clr
  Register #(.width(32)) x5 (.D(Write_Data), .en(and_5_out), .Q(x5_q), .clk(clk));  // open: clr
  Register #(.width(32)) x6 (.D(Write_Data), .en(and_6_out), .Q(x6_q), .clk(clk));  // open: clr
  Register #(.width(32)) x7 (.D(Write_Data), .en(and_7_out), .Q(x7_q), .clk(clk));  // open: clr
  Register #(.width(32)) x8 (.D(Write_Data), .en(and_8_out), .Q(x8_q), .clk(clk));  // open: clr
  Register #(.width(32)) x9 (.D(Write_Data), .en(and_9_out), .Q(x9_q), .clk(clk));  // open: clr
  Register #(.width(32)) x10 (.D(Write_Data), .en(and_3_out), .Q(x10_q), .clk(clk));  // open: clr
  Multiplexer #(.select(4), .width(32), .enable("false")) multiplexer_1 (
    .in0(x0_q), .in1(x1_q), .in2(x2_q), .in5(x5_q), .in6(x6_q), .in7(x7_q), .in8(x8_q), .in9(x9_q),
    .in10(x10_q), .out(Read_Data_1), .sel(Read__Register_1[3:0]));  // open: in3, in4, in11, in12, in13, in14, in15
  Multiplexer #(.select(4), .width(32), .enable("false")) multiplexer_2 (
    .in0(x0_q), .in1(x1_q), .in2(x2_q), .in5(x5_q), .in6(x6_q), .in7(x7_q), .in8(x8_q), .in9(x9_q),
    .in10(x10_q), .out(Read_Data_2), .sel(Read__Register_2[3:0]));  // open: in3, in4, in11, in12, in13, in14, in15

  // Other names for the same wires on the sheet: WRen = RegWEn
endmodule
