// Logisim project processor.circ as structural Verilog: 23 circuits, main circuit single_cycle
module main (
  input  [3:0] ALUSel,
  input  [31:0] A,
  input  [31:0] B,
  output OverFlow,
  output Zero,
  output [31:0] Result
);

  wire ADDoverflow, not_1_out, or_1_out;
  wire [31:0] and_1_out, mulhu_1_mulh, mulinbuilt_1_mul, mulinbuilt_1_mulh, or_2_out, sll_1_out, slt_1_out,
       sltu_1_out, sra_1_out, srl_1_out, subtractor_1_out, sum_1_result, xor_1_out;

  or or_1 (or_1_out, ALUSel[0], ALUSel[1], ALUSel[2], ALUSel[3]);
  not not_1 (not_1_out, or_1_out);
  SUM sum_1 (.A(A), .B(B), .RESULT(sum_1_result), .COUT(ADDoverflow));
  SLL sll_1 (.A(A), .B(B), .Out(sll_1_out));
  SLT slt_1 (.A(A), .B(B), .Out(slt_1_out));
  XOR xor_1 (.A(A), .B(B), .Out(xor_1_out));
  SRL srl_1 (.A(A), .B(B), .Out(srl_1_out));
  OR or_2 (.A(A), .B(B), .Out(or_2_out));
  AND and_1 (.A(A), .B(B), .Out(and_1_out));
  SRA sra_1 (.A(A), .B(B), .Out(sra_1_out));
  SLTU sltu_1 (.A(A), .B(B), .Out(sltu_1_out));
  mulinbuilt mulinbuilt_1 (.B(A), .A(B), .MUL(mulinbuilt_1_mul), .MULH(mulinbuilt_1_mulh));
  MULHU mulhu_1 (.A(A), .B(B), .MULH(mulhu_1_mulh));  // open: MULL
  Subtractor #(.width(32)) subtractor_1 (.a(A), .b(B), .out(subtractor_1_out));  // open: bin, bout
  and and_2 (OverFlow, ADDoverflow, not_1_out);
  zero_checker_a9432588 ZeroChecker (.in_1(Result), .Out(Zero));
  MUX3 mux3_1 (
    .L_0_d56634bb(sum_1_result), .L_1_db51dfe3(sll_1_out), .L_2_2b1fdd56(slt_1_out),
    .L_3_891e2c2d(sltu_1_out), .L_4_179404d2(xor_1_out), .L_5_5f174e58(srl_1_out), .L_6_f67286b0(or_2_out),
    .L_7_fb0cd3a0(and_1_out), .L_8_b104f76e(mulinbuilt_1_mul), .L_9_c7a5b8e9(mulinbuilt_1_mulh),
    .L_11_84717e35(mulhu_1_mulh), .L_12_c835480d(subtractor_1_out), .L_13_2a07598d(sra_1_out),
    .L_15_2003d26e(B), .SEL(ALUSel), .out_18(Result));  // open: L_10_ec759479, L_14_3596d129
endmodule

module zero_checker_a9432588 (
  input  [31:0] in_1,
  output Out
);

  wire or_1_out, or_2_out, or_3_out, or_4_out, or_5_out, or_6_out, or_7_out, or_8_out, or_9_out, or_10_out;

  or or_1 (or_1_out, in_1[0], in_1[1], in_1[2], in_1[3], in_1[4]);
  or or_2 (or_2_out, in_1[5], in_1[6], in_1[7], in_1[8], in_1[9]);
  or or_3 (or_3_out, in_1[10], in_1[11], in_1[12], in_1[13], in_1[14]);
  or or_4 (or_4_out, in_1[15], in_1[16], in_1[17], in_1[18], in_1[19]);
  or or_5 (or_5_out, in_1[20], in_1[21], in_1[22], in_1[23], in_1[24]);
  or or_6 (or_6_out, in_1[25], in_1[26], in_1[27], in_1[28], in_1[29]);
  or or_7 (or_7_out, in_1[30], in_1[31]);
  or or_8 (or_8_out, or_1_out, or_2_out, or_3_out, or_4_out, or_5_out);
  or or_9 (or_9_out, or_6_out, or_7_out);
  or or_10 (or_10_out, or_8_out, or_9_out);
  not not_1 (Out, or_10_out);
endmodule

module SLL (
  input  [31:0] A,
  input  [31:0] B,
  output [31:0] Out
);

  wire [4:0] bit_extender_1_out;

  Bit_Extender #(.in_width(32), .out_width(5)) bit_extender_1 (.in(B), .out(bit_extender_1_out));
  Shifter #(.width(32)) shifter_1 (.in(A), .\dist (bit_extender_1_out), .out(Out));
endmodule

module SLT (
  input  [31:0] A,
  input  [31:0] B,
  output [31:0] Out
);

  wire comparator_1_lt;

  Comparator #(.width(32)) comparator_1 (.a(A), .b(B), .lt(comparator_1_lt));  // open: gt, eq
  assign Out = {{31{comparator_1_lt}}, comparator_1_lt};  // Bit_Extender bit_extender_1
endmodule

module XOR (
  input  [31:0] A,
  input  [31:0] B,
  output [31:0] Out
);

  xor xor_1 (Out[0], A[0], B[0]);
  xor xor_2 (Out[1], A[1], B[1]);
  xor xor_3 (Out[2], A[2], B[2]);
  xor xor_4 (Out[3], A[3], B[3]);
  xor xor_5 (Out[4], A[4], B[4]);
  xor xor_6 (Out[5], A[5], B[5]);
  xor xor_7 (Out[6], A[6], B[6]);
  xor xor_8 (Out[7], A[7], B[7]);
  xor xor_9 (Out[8], A[8], B[8]);
  xor xor_10 (Out[9], A[9], B[9]);
  xor xor_11 (Out[10], A[10], B[10]);
  xor xor_12 (Out[11], A[11], B[11]);
  xor xor_13 (Out[12], A[12], B[12]);
  xor xor_14 (Out[13], A[13], B[13]);
  xor xor_15 (Out[14], A[14], B[14]);
  xor xor_16 (Out[15], A[15], B[15]);
  xor xor_17 (Out[16], A[16], B[16]);
  xor xor_18 (Out[17], A[17], B[17]);
  xor xor_19 (Out[18], A[18], B[18]);
  xor xor_20 (Out[19], A[19], B[19]);
  xor xor_21 (Out[20], A[20], B[20]);
  xor xor_22 (Out[21], A[21], B[21]);
  xor xor_23 (Out[22], A[22], B[22]);
  xor xor_24 (Out[23], A[23], B[23]);
  xor xor_25 (Out[24], A[24], B[24]);
  xor xor_26 (Out[25], A[25], B[25]);
  xor xor_27 (Out[26], A[26], B[26]);
  xor xor_28 (Out[27], A[27], B[27]);
  xor xor_29 (Out[28], A[28], B[28]);
  xor xor_30 (Out[29], A[29], B[29]);
  xor xor_31 (Out[30], A[30], B[30]);
  xor xor_32 (Out[31], A[31], B[31]);
endmodule

module SRL (
  input  [31:0] A,
  input  [31:0] B,
  output [31:0] Out
);

  wire [4:0] bit_extender_1_out;

  Bit_Extender #(.in_width(32), .out_width(5)) bit_extender_1 (.in(B), .out(bit_extender_1_out));
  Shifter #(.shift("lr"), .width(32)) shifter_1 (.in(A), .\dist (bit_extender_1_out), .out(Out));
endmodule

module OR (
  input  [31:0] A,
  input  [31:0] B,
  output [31:0] Out
);

  or or_1 (Out[0], A[0], B[0]);
  or or_2 (Out[1], A[1], B[1]);
  or or_3 (Out[2], A[2], B[2]);
  or or_4 (Out[3], A[3], B[3]);
  or or_5 (Out[4], A[4], B[4]);
  or or_6 (Out[5], A[5], B[5]);
  or or_7 (Out[6], A[6], B[6]);
  or or_8 (Out[7], A[7], B[7]);
  or or_9 (Out[8], A[8], B[8]);
  or or_10 (Out[9], A[9], B[9]);
  or or_11 (Out[10], A[10], B[10]);
  or or_12 (Out[11], A[11], B[11]);
  or or_13 (Out[12], A[12], B[12]);
  or or_14 (Out[13], A[13], B[13]);
  or or_15 (Out[14], A[14], B[14]);
  or or_16 (Out[15], A[15], B[15]);
  or or_17 (Out[16], A[16], B[16]);
  or or_18 (Out[17], A[17], B[17]);
  or or_19 (Out[18], A[18], B[18]);
  or or_20 (Out[19], A[19], B[19]);
  or or_21 (Out[20], A[20], B[20]);
  or or_22 (Out[21], A[21], B[21]);
  or or_23 (Out[22], A[22], B[22]);
  or or_24 (Out[23], A[23], B[23]);
  or or_25 (Out[24], A[24], B[24]);
  or or_26 (Out[25], A[25], B[25]);
  or or_27 (Out[26], A[26], B[26]);
  or or_28 (Out[27], A[27], B[27]);
  or or_29 (Out[28], A[28], B[28]);
  or or_30 (Out[29], A[29], B[29]);
  or or_31 (Out[30], A[30], B[30]);
  or or_32 (Out[31], A[31], B[31]);
endmodule

module AND (
  input  [31:0] A,
  input  [31:0] B,
  output [31:0] Out
);

  and and_1 (Out[0], A[0], B[0]);
  and and_2 (Out[1], A[1], B[1]);
  and and_3 (Out[2], A[2], B[2]);
  and and_4 (Out[3], A[3], B[3]);
  and and_5 (Out[4], A[4], B[4]);
  and and_6 (Out[5], A[5], B[5]);
  and and_7 (Out[6], A[6], B[6]);
  and and_8 (Out[7], A[7], B[7]);
  and and_9 (Out[8], A[8], B[8]);
  and and_10 (Out[9], A[9], B[9]);
  and and_11 (Out[10], A[10], B[10]);
  and and_12 (Out[11], A[11], B[11]);
  and and_13 (Out[12], A[12], B[12]);
  and and_14 (Out[13], A[13], B[13]);
  and and_15 (Out[14], A[14], B[14]);
  and and_16 (Out[15], A[15], B[15]);
  and and_17 (Out[16], A[16], B[16]);
  and and_18 (Out[17], A[17], B[17]);
  and and_19 (Out[18], A[18], B[18]);
  and and_20 (Out[19], A[19], B[19]);
  and and_21 (Out[20], A[20], B[20]);
  and and_22 (Out[21], A[21], B[21]);
  and and_23 (Out[22], A[22], B[22]);
  and and_24 (Out[23], A[23], B[23]);
  and and_25 (Out[24], A[24], B[24]);
  and and_26 (Out[25], A[25], B[25]);
  and and_27 (Out[26], A[26], B[26]);
  and and_28 (Out[27], A[27], B[27]);
  and and_29 (Out[28], A[28], B[28]);
  and and_30 (Out[29], A[29], B[29]);
  and and_31 (Out[30], A[30], B[30]);
  and and_32 (Out[31], A[31], B[31]);
endmodule

module SRA (
  input  [31:0] A,
  input  [31:0] B,
  output [31:0] Out
);

  wire [4:0] bit_extender_1_out;

  Bit_Extender #(.in_width(32), .out_width(5)) bit_extender_1 (.in(B), .out(bit_extender_1_out));
  Shifter #(.shift("ar"), .width(32)) shifter_1 (.in(A), .\dist (bit_extender_1_out), .out(Out));
endmodule

module MULHU (
  input  [31:0] A,
  input  [31:0] B,
  output [31:0] MULH,
  output [31:0] MULL
);

  wire [31:0] bit_extender_1_out, bit_extender_2_out, bit_extender_3_out, bit_extender_4_out,
       bit_extender_5_out, bit_extender_6_out, bit_extender_7_out, bit_extender_8_out, bit_extender_9_out,
       bit_extender_10_out, bit_extender_11_out, bit_extender_12_out, bit_extender_13_out,
       bit_extender_14_out, bit_extender_15_out, bit_extender_16_out, bit_extender_17_out,
       bit_extender_18_out, bit_extender_19_out, bit_extender_20_out, bit_extender_21_out,
       bit_extender_22_out, bit_extender_23_out, bit_extender_24_out, bit_extender_25_out,
       bit_extender_26_out, bit_extender_27_out, bit_extender_28_out, bit_extender_29_out,
       bit_extender_30_out, bit_extender_31_out, bit_extender_32_out, bit_extender_33_out, mulhuhelper_2_c,
       mulhuhelper_3_c, mulhuhelper_4_c, mulhuhelper_5_c, mulhuhelper_6_c, mulhuhelper_7_c, mulhuhelper_8_c,
       mulhuhelper_9_c, mulhuhelper_10_c, mulhuhelper_11_c, mulhuhelper_12_c, mulhuhelper_13_c,
       mulhuhelper_14_c, mulhuhelper_15_c, mulhuhelper_16_c, mulhuhelper_17_c, mulhuhelper_18_c,
       mulhuhelper_19_c, mulhuhelper_20_c, mulhuhelper_21_c, mulhuhelper_22_c, mulhuhelper_23_c,
       mulhuhelper_24_c, mulhuhelper_25_c, mulhuhelper_26_c, mulhuhelper_27_c, mulhuhelper_28_c,
       mulhuhelper_29_c, mulhuhelper_30_c, mulhuhelper_31_c, mulhuhelper_32_c;
  wire [31:1] adder_1_out, adder_2_out, adder_3_out, adder_4_out, adder_5_out, adder_6_out, adder_7_out,
       adder_8_out, adder_9_out, adder_10_out, adder_11_out, adder_12_out, adder_13_out, adder_14_out,
       adder_15_out, adder_16_out, adder_17_out, adder_18_out, adder_19_out, adder_20_out, adder_21_out,
       adder_22_out, adder_23_out, adder_24_out, adder_25_out, adder_26_out, adder_27_out, adder_28_out,
       adder_29_out, adder_30_out, mulhuhelper_1_c;
  wire [31:31] adder_1_cout, adder_2_cout, adder_3_cout, adder_4_cout, adder_5_cout, adder_6_cout,
       adder_7_cout, adder_8_cout, adder_9_cout, adder_10_cout, adder_11_cout, adder_12_cout, adder_13_cout,
       adder_14_cout, adder_15_cout, adder_16_cout, adder_17_cout, adder_18_cout, adder_19_cout,
       adder_20_cout, adder_21_cout, adder_22_cout, adder_23_cout, adder_24_cout, adder_25_cout,
       adder_26_cout, adder_27_cout, adder_28_cout, adder_29_cout, adder_30_cout;

  MULHUhelper mulhuhelper_1 (.A(A), .B(bit_extender_1_out), .C({mulhuhelper_1_c, MULL[0]}));
  assign bit_extender_1_out = {{31{B[0]}}, B[0]};  // Bit_Extender bit_extender_1
  MULHUhelper mulhuhelper_2 (.A(A), .B(bit_extender_2_out), .C(mulhuhelper_2_c));
  assign bit_extender_2_out = {{31{B[1]}}, B[1]};  // Bit_Extender bit_extender_2
  MULHUhelper mulhuhelper_3 (.A(A), .B(bit_extender_3_out), .C(mulhuhelper_3_c));
  assign bit_extender_3_out = {{31{B[2]}}, B[2]};  // Bit_Extender bit_extender_3
  MULHUhelper mulhuhelper_4 (.A(A), .B(bit_extender_4_out), .C(mulhuhelper_4_c));
  assign bit_extender_4_out = {{31{B[3]}}, B[3]};  // Bit_Extender bit_extender_4
  MULHUhelper mulhuhelper_5 (.A(A), .B(bit_extender_5_out), .C(mulhuhelper_5_c));
  assign bit_extender_5_out = {{31{B[4]}}, B[4]};  // Bit_Extender bit_extender_5
  MULHUhelper mulhuhelper_6 (.A(A), .B(bit_extender_6_out), .C(mulhuhelper_6_c));
  assign bit_extender_6_out = {{31{B[5]}}, B[5]};  // Bit_Extender bit_extender_6
  MULHUhelper mulhuhelper_7 (.A(A), .B(bit_extender_7_out), .C(mulhuhelper_7_c));
  assign bit_extender_7_out = {{31{B[6]}}, B[6]};  // Bit_Extender bit_extender_7
  MULHUhelper mulhuhelper_8 (.A(A), .B(bit_extender_8_out), .C(mulhuhelper_8_c));
  assign bit_extender_8_out = {{31{B[7]}}, B[7]};  // Bit_Extender bit_extender_8
  MULHUhelper mulhuhelper_9 (.A(A), .B(bit_extender_9_out), .C(mulhuhelper_9_c));
  assign bit_extender_9_out = {{31{B[8]}}, B[8]};  // Bit_Extender bit_extender_9
  MULHUhelper mulhuhelper_10 (.A(A), .B(bit_extender_10_out), .C(mulhuhelper_10_c));
  assign bit_extender_10_out = {{31{B[9]}}, B[9]};  // Bit_Extender bit_extender_10
  MULHUhelper mulhuhelper_11 (.A(A), .B(bit_extender_11_out), .C(mulhuhelper_11_c));
  assign bit_extender_11_out = {{31{B[10]}}, B[10]};  // Bit_Extender bit_extender_11
  MULHUhelper mulhuhelper_12 (.A(A), .B(bit_extender_12_out), .C(mulhuhelper_12_c));
  assign bit_extender_12_out = {{31{B[11]}}, B[11]};  // Bit_Extender bit_extender_12
  MULHUhelper mulhuhelper_13 (.A(A), .B(bit_extender_13_out), .C(mulhuhelper_13_c));
  assign bit_extender_13_out = {{31{B[12]}}, B[12]};  // Bit_Extender bit_extender_13
  MULHUhelper mulhuhelper_14 (.A(A), .B(bit_extender_14_out), .C(mulhuhelper_14_c));
  assign bit_extender_14_out = {{31{B[13]}}, B[13]};  // Bit_Extender bit_extender_14
  MULHUhelper mulhuhelper_15 (.A(A), .B(bit_extender_15_out), .C(mulhuhelper_15_c));
  assign bit_extender_15_out = {{31{B[14]}}, B[14]};  // Bit_Extender bit_extender_15
  MULHUhelper mulhuhelper_16 (.A(A), .B(bit_extender_16_out), .C(mulhuhelper_16_c));
  assign bit_extender_16_out = {{31{B[15]}}, B[15]};  // Bit_Extender bit_extender_16
  MULHUhelper mulhuhelper_17 (.A(A), .B(bit_extender_17_out), .C(mulhuhelper_17_c));
  assign bit_extender_17_out = {{31{B[16]}}, B[16]};  // Bit_Extender bit_extender_17
  MULHUhelper mulhuhelper_18 (.A(A), .B(bit_extender_18_out), .C(mulhuhelper_18_c));
  assign bit_extender_18_out = {{31{B[17]}}, B[17]};  // Bit_Extender bit_extender_18
  MULHUhelper mulhuhelper_19 (.A(A), .B(bit_extender_19_out), .C(mulhuhelper_19_c));
  assign bit_extender_19_out = {{31{B[18]}}, B[18]};  // Bit_Extender bit_extender_19
  MULHUhelper mulhuhelper_20 (.A(A), .B(bit_extender_20_out), .C(mulhuhelper_20_c));
  assign bit_extender_20_out = {{31{B[19]}}, B[19]};  // Bit_Extender bit_extender_20
  MULHUhelper mulhuhelper_21 (.A(A), .B(bit_extender_21_out), .C(mulhuhelper_21_c));
  assign bit_extender_21_out = {{31{B[20]}}, B[20]};  // Bit_Extender bit_extender_21
  MULHUhelper mulhuhelper_22 (.A(A), .B(bit_extender_22_out), .C(mulhuhelper_22_c));
  assign bit_extender_22_out = {{31{B[21]}}, B[21]};  // Bit_Extender bit_extender_22
  MULHUhelper mulhuhelper_23 (.A(A), .B(bit_extender_23_out), .C(mulhuhelper_23_c));
  assign bit_extender_23_out = {{31{B[22]}}, B[22]};  // Bit_Extender bit_extender_23
  MULHUhelper mulhuhelper_24 (.A(A), .B(bit_extender_24_out), .C(mulhuhelper_24_c));
  assign bit_extender_24_out = {{31{B[23]}}, B[23]};  // Bit_Extender bit_extender_24
  MULHUhelper mulhuhelper_25 (.A(A), .B(bit_extender_25_out), .C(mulhuhelper_25_c));
  assign bit_extender_25_out = {{31{B[24]}}, B[24]};  // Bit_Extender bit_extender_25
  MULHUhelper mulhuhelper_26 (.A(A), .B(bit_extender_26_out), .C(mulhuhelper_26_c));
  assign bit_extender_26_out = {{31{B[25]}}, B[25]};  // Bit_Extender bit_extender_26
  MULHUhelper mulhuhelper_27 (.A(A), .B(bit_extender_27_out), .C(mulhuhelper_27_c));
  assign bit_extender_27_out = {{31{B[26]}}, B[26]};  // Bit_Extender bit_extender_27
  MULHUhelper mulhuhelper_28 (.A(A), .B(bit_extender_28_out), .C(mulhuhelper_28_c));
  assign bit_extender_28_out = {{31{B[27]}}, B[27]};  // Bit_Extender bit_extender_28
  MULHUhelper mulhuhelper_29 (.A(A), .B(bit_extender_29_out), .C(mulhuhelper_29_c));
  assign bit_extender_29_out = {{31{B[28]}}, B[28]};  // Bit_Extender bit_extender_29
  MULHUhelper mulhuhelper_30 (.A(A), .B(bit_extender_30_out), .C(mulhuhelper_30_c));
  assign bit_extender_30_out = {{31{B[29]}}, B[29]};  // Bit_Extender bit_extender_30
  MULHUhelper mulhuhelper_31 (.A(A), .B(bit_extender_31_out), .C(mulhuhelper_31_c));
  assign bit_extender_31_out = {{31{B[30]}}, B[30]};  // Bit_Extender bit_extender_31
  MULHUhelper mulhuhelper_32 (.A(A), .B(bit_extender_32_out), .C(mulhuhelper_32_c));
  assign bit_extender_32_out = {{31{B[31]}}, B[31]};  // Bit_Extender bit_extender_32
  // Probe on bit_extender_33_out
  assign bit_extender_33_out = {{1{mulhuhelper_1_c[31]}}, mulhuhelper_1_c};  // Bit_Extender bit_extender_33
  Adder #(.width(32)) adder_1 (
    .a(bit_extender_33_out), .b(mulhuhelper_2_c), .out({adder_1_out, MULL[1]}), .cout(adder_1_cout[31]));  // open: cin
  Adder #(.width(32)) adder_2 (
    .a({adder_1_cout[31], adder_1_out}), .b(mulhuhelper_3_c), .out({adder_2_out, MULL[2]}),
    .cout(adder_2_cout[31]));  // open: cin
  Adder #(.width(32)) adder_3 (
    .a({adder_2_cout[31], adder_2_out}), .b(mulhuhelper_4_c), .out({adder_3_out, MULL[3]}),
    .cout(adder_3_cout[31]));  // open: cin
  Adder #(.width(32)) adder_4 (
    .a({adder_3_cout[31], adder_3_out}), .b(mulhuhelper_5_c), .out({adder_4_out, MULL[4]}),
    .cout(adder_4_cout[31]));  // open: cin
  Adder #(.width(32)) adder_5 (
    .a({adder_4_cout[31], adder_4_out}), .b(mulhuhelper_6_c), .out({adder_5_out, MULL[5]}),
    .cout(adder_5_cout[31]));  // open: cin
  Adder #(.width(32)) adder_6 (
    .a({adder_5_cout[31], adder_5_out}), .b(mulhuhelper_7_c), .out({adder_6_out, MULL[6]}),
    .cout(adder_6_cout[31]));  // open: cin
  Adder #(.width(32)) adder_7 (
    .a({adder_6_cout[31], adder_6_out}), .b(mulhuhelper_8_c), .out({adder_7_out, MULL[7]}),
    .cout(adder_7_cout[31]));  // open: cin
  Adder #(.width(32)) adder_8 (
    .a({adder_7_cout[31], adder_7_out}), .b(mulhuhelper_9_c), .out({adder_8_out, MULL[8]}),
    .cout(adder_8_cout[31]));  // open: cin
  Adder #(.width(32)) adder_9 (
    .a({adder_8_cout[31], adder_8_out}), .b(mulhuhelper_10_c), .out({adder_9_out, MULL[9]}),
    .cout(adder_9_cout[31]));  // open: cin
  Adder #(.width(32)) adder_10 (
    .a({adder_9_cout[31], adder_9_out}), .b(mulhuhelper_11_c), .out({adder_10_out, MULL[10]}),
    .cout(adder_10_cout[31]));  // open: cin
  Adder #(.width(32)) adder_11 (
    .a({adder_10_cout[31], adder_10_out}), .b(mulhuhelper_12_c), .out({adder_11_out, MULL[11]}),
    .cout(adder_11_cout[31]));  // open: cin
  Adder #(.width(32)) adder_12 (
    .a({adder_11_cout[31], adder_11_out}), .b(mulhuhelper_13_c), .out({adder_12_out, MULL[12]}),
    .cout(adder_12_cout[31]));  // open: cin
  Adder #(.width(32)) adder_13 (
    .a({adder_12_cout[31], adder_12_out}), .b(mulhuhelper_14_c), .out({adder_13_out, MULL[13]}),
    .cout(adder_13_cout[31]));  // open: cin
  Adder #(.width(32)) adder_14 (
    .a({adder_13_cout[31], adder_13_out}), .b(mulhuhelper_15_c), .out({adder_14_out, MULL[14]}),
    .cout(adder_14_cout[31]));  // open: cin
  Adder #(.width(32)) adder_15 (
    .a({adder_14_cout[31], adder_14_out}), .b(mulhuhelper_16_c), .out({adder_15_out, MULL[15]}),
    .cout(adder_15_cout[31]));  // open: cin
  Adder #(.width(32)) adder_16 (
    .a({adder_15_cout[31], adder_15_out}), .b(mulhuhelper_17_c), .out({adder_16_out, MULL[16]}),
    .cout(adder_16_cout[31]));  // open: cin
  Adder #(.width(32)) adder_17 (
    .a({adder_16_cout[31], adder_16_out}), .b(mulhuhelper_18_c), .out({adder_17_out, MULL[17]}),
    .cout(adder_17_cout[31]));  // open: cin
  Adder #(.width(32)) adder_18 (
    .a({adder_17_cout[31], adder_17_out}), .b(mulhuhelper_19_c), .out({adder_18_out, MULL[18]}),
    .cout(adder_18_cout[31]));  // open: cin
  Adder #(.width(32)) adder_19 (
    .a({adder_18_cout[31], adder_18_out}), .b(mulhuhelper_20_c), .out({adder_19_out, MULL[19]}),
    .cout(adder_19_cout[31]));  // open: cin
  Adder #(.width(32)) adder_20 (
    .a({adder_19_cout[31], adder_19_out}), .b(mulhuhelper_21_c), .out({adder_20_out, MULL[20]}),
    .cout(adder_20_cout[31]));  // open: cin
  Adder #(.width(32)) adder_21 (
    .a({adder_20_cout[31], adder_20_out}), .b(mulhuhelper_22_c), .out({adder_21_out, MULL[21]}),
    .cout(adder_21_cout[31]));  // open: cin
  Adder #(.width(32)) adder_22 (
    .a({adder_21_cout[31], adder_21_out}), .b(mulhuhelper_23_c), .out({adder_22_out, MULL[22]}),
    .cout(adder_22_cout[31]));  // open: cin
  Adder #(.width(32)) adder_23 (
    .a({adder_22_cout[31], adder_22_out}), .b(mulhuhelper_24_c), .out({adder_23_out, MULL[23]}),
    .cout(adder_23_cout[31]));  // open: cin
  Adder #(.width(32)) adder_24 (
    .a({adder_23_cout[31], adder_23_out}), .b(mulhuhelper_25_c), .out({adder_24_out, MULL[24]}),
    .cout(adder_24_cout[31]));  // open: cin
  Adder #(.width(32)) adder_25 (
    .a({adder_24_cout[31], adder_24_out}), .b(mulhuhelper_26_c), .out({adder_25_out, MULL[25]}),
    .cout(adder_25_cout[31]));  // open: cin
  Adder #(.width(32)) adder_26 (
    .a({adder_25_cout[31], adder_25_out}), .b(mulhuhelper_27_c), .out({adder_26_out, MULL[26]}),
    .cout(adder_26_cout[31]));  // open: cin
  Adder #(.width(32)) adder_27 (
    .a({adder_26_cout[31], adder_26_out}), .b(mulhuhelper_28_c), .out({adder_27_out, MULL[27]}),
    .cout(adder_27_cout[31]));  // open: cin
  Adder #(.width(32)) adder_28 (
    .a({adder_27_cout[31], adder_27_out}), .b(mulhuhelper_29_c), .out({adder_28_out, MULL[28]}),
    .cout(adder_28_cout[31]));  // open: cin
  Adder #(.width(32)) adder_29 (
    .a({adder_28_cout[31], adder_28_out}), .b(mulhuhelper_30_c), .out({adder_29_out, MULL[29]}),
    .cout(adder_29_cout[31]));  // open: cin
  Adder #(.width(32)) adder_30 (
    .a({adder_29_cout[31], adder_29_out}), .b(mulhuhelper_31_c), .out({adder_30_out, MULL[30]}),
    .cout(adder_30_cout[31]));  // open: cin
  Adder #(.width(32)) adder_31 (
    .a({adder_30_cout[31], adder_30_out}), .b(mulhuhelper_32_c), .out({MULH[30:0], MULL[31]}), .cout(MULH[31]));  // open: cin

  // Other names for the same wires on the sheet: R0 = MULL[0]; RL[31:0] = MULL; R1 = MULL[1]; R2 = MULL[2];
  //   R3 = MULL[3]; R4 = MULL[4]; R5 = MULL[5]; R6 = MULL[6]; R7 = MULL[7]; R8 = MULL[8]; R9 = MULL[9];
  //   R10 = MULL[10]; R11 = MULL[11]; R12 = MULL[12]; R13 = MULL[13]; R14 = MULL[14]; R15 = MULL[15]; R16 = MULL[16];
  //   R17 = MULL[17]; R18 = MULL[18]; R19 = MULL[19]; R20 = MULL[20]; R21 = MULL[21]; R22 = MULL[22]; R23 = MULL[23];
  //   R24 = MULL[24]; R25 = MULL[25]; R26 = MULL[26]; R27 = MULL[27]; R28 = MULL[28]; R29 = MULL[29]; R30 = MULL[30];
  //   R31 = MULL[31]; RU[31:0] = MULH
endmodule

module MULHUhelper (
  input  [31:0] A,
  input  [31:0] B,
  output [31:0] C
);

  Multiplier #(.width(32)) multiplier_1 (.a(A), .b(B), .out(C));  // open: cin, cout
endmodule

module MUX1 (
  input  in_1,
  input  in_2,
  input  in_3,
  input  in_4,
  input  in_5,
  input  in_6,
  output out_7
);

  wire and_1_out, and_2_out, and_3_out, and_4_out, not_1_out, not_2_out;

  not not_1 (not_1_out, in_5);
  not not_2 (not_2_out, in_6);
  and and_1 (and_1_out, in_1, in_5, in_6);
  and and_2 (and_2_out, in_2, not_1_out, in_6);
  and and_3 (and_3_out, in_3, in_5, not_2_out);
  and and_4 (and_4_out, in_4, not_1_out, not_2_out);
  or or_1 (out_7, and_1_out, and_2_out, and_3_out, and_4_out);
endmodule

module MUX2 (
  input  [31:0] in_1,
  input  [31:0] in_2,
  input  [31:0] in_3,
  input  [31:0] in_4,
  input  in_5,
  input  in_6,
  output [31:0] out_7
);

  MUX1 mux1_1 (
    .in_1(in_1[0]), .in_2(in_2[0]), .in_3(in_3[0]), .in_4(in_4[0]), .in_5(in_5), .in_6(in_6), .out_7(out_7[0]));
  MUX1 mux1_2 (
    .in_1(in_1[1]), .in_2(in_2[1]), .in_3(in_3[1]), .in_4(in_4[1]), .in_5(in_5), .in_6(in_6), .out_7(out_7[1]));
  MUX1 mux1_3 (
    .in_1(in_1[2]), .in_2(in_2[2]), .in_3(in_3[2]), .in_4(in_4[2]), .in_5(in_5), .in_6(in_6), .out_7(out_7[2]));
  MUX1 mux1_4 (
    .in_1(in_1[3]), .in_2(in_2[3]), .in_3(in_3[3]), .in_4(in_4[3]), .in_5(in_5), .in_6(in_6), .out_7(out_7[3]));
  MUX1 mux1_5 (
    .in_1(in_1[4]), .in_2(in_2[4]), .in_3(in_3[4]), .in_4(in_4[4]), .in_5(in_5), .in_6(in_6), .out_7(out_7[4]));
  MUX1 mux1_6 (
    .in_1(in_1[5]), .in_2(in_2[5]), .in_3(in_3[5]), .in_4(in_4[5]), .in_5(in_5), .in_6(in_6), .out_7(out_7[5]));
  MUX1 mux1_7 (
    .in_1(in_1[6]), .in_2(in_2[6]), .in_3(in_3[6]), .in_4(in_4[6]), .in_5(in_5), .in_6(in_6), .out_7(out_7[6]));
  MUX1 mux1_8 (
    .in_1(in_1[7]), .in_2(in_2[7]), .in_3(in_3[7]), .in_4(in_4[7]), .in_5(in_5), .in_6(in_6), .out_7(out_7[7]));
  MUX1 mux1_9 (
    .in_1(in_1[8]), .in_2(in_2[8]), .in_3(in_3[8]), .in_4(in_4[8]), .in_5(in_5), .in_6(in_6), .out_7(out_7[8]));
  MUX1 mux1_10 (
    .in_1(in_1[9]), .in_2(in_2[9]), .in_3(in_3[9]), .in_4(in_4[9]), .in_5(in_5), .in_6(in_6), .out_7(out_7[9]));
  MUX1 mux1_11 (
    .in_1(in_1[10]), .in_2(in_2[10]), .in_3(in_3[10]), .in_4(in_4[10]), .in_5(in_5), .in_6(in_6),
    .out_7(out_7[10]));
  MUX1 mux1_12 (
    .in_1(in_1[11]), .in_2(in_2[11]), .in_3(in_3[11]), .in_4(in_4[11]), .in_5(in_5), .in_6(in_6),
    .out_7(out_7[11]));
  MUX1 mux1_13 (
    .in_1(in_1[12]), .in_2(in_2[12]), .in_3(in_3[12]), .in_4(in_4[12]), .in_5(in_5), .in_6(in_6),
    .out_7(out_7[12]));
  MUX1 mux1_14 (
    .in_1(in_1[13]), .in_2(in_2[13]), .in_3(in_3[13]), .in_4(in_4[13]), .in_5(in_5), .in_6(in_6),
    .out_7(out_7[13]));
  MUX1 mux1_15 (
    .in_1(in_1[14]), .in_2(in_2[14]), .in_3(in_3[14]), .in_4(in_4[14]), .in_5(in_5), .in_6(in_6),
    .out_7(out_7[14]));
  MUX1 mux1_16 (
    .in_1(in_1[15]), .in_2(in_2[15]), .in_3(in_3[15]), .in_4(in_4[15]), .in_5(in_5), .in_6(in_6),
    .out_7(out_7[15]));
  MUX1 mux1_17 (
    .in_1(in_1[16]), .in_2(in_2[16]), .in_3(in_3[16]), .in_4(in_4[16]), .in_5(in_5), .in_6(in_6),
    .out_7(out_7[16]));
  MUX1 mux1_18 (
    .in_1(in_1[17]), .in_2(in_2[17]), .in_3(in_3[17]), .in_4(in_4[17]), .in_5(in_5), .in_6(in_6),
    .out_7(out_7[17]));
  MUX1 mux1_19 (
    .in_1(in_1[18]), .in_2(in_2[18]), .in_3(in_3[18]), .in_4(in_4[18]), .in_5(in_5), .in_6(in_6),
    .out_7(out_7[18]));
  MUX1 mux1_20 (
    .in_1(in_1[19]), .in_2(in_2[19]), .in_3(in_3[19]), .in_4(in_4[19]), .in_5(in_5), .in_6(in_6),
    .out_7(out_7[19]));
  MUX1 mux1_21 (
    .in_1(in_1[20]), .in_2(in_2[20]), .in_3(in_3[20]), .in_4(in_4[20]), .in_5(in_5), .in_6(in_6),
    .out_7(out_7[20]));
  MUX1 mux1_22 (
    .in_1(in_1[21]), .in_2(in_2[21]), .in_3(in_3[21]), .in_4(in_4[21]), .in_5(in_5), .in_6(in_6),
    .out_7(out_7[21]));
  MUX1 mux1_23 (
    .in_1(in_1[22]), .in_2(in_2[22]), .in_3(in_3[22]), .in_4(in_4[22]), .in_5(in_5), .in_6(in_6),
    .out_7(out_7[22]));
  MUX1 mux1_24 (
    .in_1(in_1[23]), .in_2(in_2[23]), .in_3(in_3[23]), .in_4(in_4[23]), .in_5(in_5), .in_6(in_6),
    .out_7(out_7[23]));
  MUX1 mux1_25 (
    .in_1(in_1[24]), .in_2(in_2[24]), .in_3(in_3[24]), .in_4(in_4[24]), .in_5(in_5), .in_6(in_6),
    .out_7(out_7[24]));
  MUX1 mux1_26 (
    .in_1(in_1[25]), .in_2(in_2[25]), .in_3(in_3[25]), .in_4(in_4[25]), .in_5(in_5), .in_6(in_6),
    .out_7(out_7[25]));
  MUX1 mux1_27 (
    .in_1(in_1[26]), .in_2(in_2[26]), .in_3(in_3[26]), .in_4(in_4[26]), .in_5(in_5), .in_6(in_6),
    .out_7(out_7[26]));
  MUX1 mux1_28 (
    .in_1(in_1[27]), .in_2(in_2[27]), .in_3(in_3[27]), .in_4(in_4[27]), .in_5(in_5), .in_6(in_6),
    .out_7(out_7[27]));
  MUX1 mux1_29 (
    .in_1(in_1[28]), .in_2(in_2[28]), .in_3(in_3[28]), .in_4(in_4[28]), .in_5(in_5), .in_6(in_6),
    .out_7(out_7[28]));
  MUX1 mux1_30 (
    .in_1(in_1[29]), .in_2(in_2[29]), .in_3(in_3[29]), .in_4(in_4[29]), .in_5(in_5), .in_6(in_6),
    .out_7(out_7[29]));
  MUX1 mux1_31 (
    .in_1(in_1[30]), .in_2(in_2[30]), .in_3(in_3[30]), .in_4(in_4[30]), .in_5(in_5), .in_6(in_6),
    .out_7(out_7[30]));
  MUX1 mux1_32 (
    .in_1(in_1[31]), .in_2(in_2[31]), .in_3(in_3[31]), .in_4(in_4[31]), .in_5(in_5), .in_6(in_6),
    .out_7(out_7[31]));

  // Other names for the same wires on the sheet: a0 = in_1[0]; a1 = in_1[1]; a2 = in_1[2]; a3 = in_1[3]; a4 = in_1[4];
  //   a5 = in_1[5]; a6 = in_1[6]; a7 = in_1[7]; a8 = in_1[8]; a9 = in_1[9]; a10 = in_1[10]; a11 = in_1[11];
  //   a12 = in_1[12]; a13 = in_1[13]; a14 = in_1[14]; a15 = in_1[15]; a16 = in_1[16]; a17 = in_1[17]; a18 = in_1[18];
  //   a19 = in_1[19]; a20 = in_1[20]; a21 = in_1[21]; a22 = in_1[22]; a23 = in_1[23]; a24 = in_1[24]; a25 = in_1[25];
  //   a26 = in_1[26]; a27 = in_1[27]; a28 = in_1[28]; a29 = in_1[29]; a30 = in_1[30]; a31 = in_1[31]; b0 = in_2[0];
  //   b1 = in_2[1]; b2 = in_2[2]; b3 = in_2[3]; b4 = in_2[4]; b5 = in_2[5]; b6 = in_2[6]; b7 = in_2[7]; b8 = in_2[8];
  //   b9 = in_2[9]; b10 = in_2[10]; b11 = in_2[11]; b12 = in_2[12]; b13 = in_2[13]; b14 = in_2[14]; b15 = in_2[15];
  //   b16 = in_2[16]; b17 = in_2[17]; b18 = in_2[18]; b19 = in_2[19]; b20 = in_2[20]; b21 = in_2[21]; b22 = in_2[22];
  //   b23 = in_2[23]; b24 = in_2[24]; b25 = in_2[25]; b26 = in_2[26]; b27 = in_2[27]; b28 = in_2[28]; b29 = in_2[29];
  //   b30 = in_2[30]; b31 = in_2[31]; c0 = in_3[0]; c1 = in_3[1]; c2 = in_3[2]; c3 = in_3[3]; c4 = in_3[4];
  //   c5 = in_3[5]; c6 = in_3[6]; c7 = in_3[7]; c8 = in_3[8]; c9 = in_3[9]; c10 = in_3[10]; c11 = in_3[11];
  //   c12 = in_3[12]; c13 = in_3[13]; c14 = in_3[14]; c15 = in_3[15]; c16 = in_3[16]; c17 = in_3[17]; c18 = in_3[18];
  //   c19 = in_3[19]; c20 = in_3[20]; c21 = in_3[21]; c22 = in_3[22]; c23 = in_3[23]; c24 = in_3[24]; c25 = in_3[25];
  //   c26 = in_3[26]; c27 = in_3[27]; c28 = in_3[28]; c29 = in_3[29]; c30 = in_3[30]; c31 = in_3[31]; d0 = in_4[0];
  //   d1 = in_4[1]; d2 = in_4[2]; d3 = in_4[3]; d4 = in_4[4]; d5 = in_4[5]; d6 = in_4[6]; d7 = in_4[7]; d8 = in_4[8];
  //   d9 = in_4[9]; d10 = in_4[10]; d11 = in_4[11]; d12 = in_4[12]; d13 = in_4[13]; d14 = in_4[14]; d15 = in_4[15];
  //   d16 = in_4[16]; d17 = in_4[17]; d18 = in_4[18]; d19 = in_4[19]; d20 = in_4[20]; d21 = in_4[21]; d22 = in_4[22];
  //   d23 = in_4[23]; d24 = in_4[24]; d25 = in_4[25]; d26 = in_4[26]; d27 = in_4[27]; d28 = in_4[28]; d29 = in_4[29];
  //   d30 = in_4[30]; d31 = in_4[31]
endmodule

module MUX3 (
  input  [31:0] L_0_d56634bb,
  input  [31:0] L_1_db51dfe3,
  input  [31:0] L_2_2b1fdd56,
  input  [31:0] L_3_891e2c2d,
  input  [31:0] L_4_179404d2,
  input  [31:0] L_5_5f174e58,
  input  [31:0] L_6_f67286b0,
  input  [31:0] L_7_fb0cd3a0,
  input  [31:0] L_8_b104f76e,
  input  [31:0] L_9_c7a5b8e9,
  input  [31:0] L_10_ec759479,
  input  [31:0] L_11_84717e35,
  input  [31:0] L_12_c835480d,
  input  [31:0] L_13_2a07598d,
  input  [31:0] L_14_3596d129,
  input  [31:0] L_15_2003d26e,
  input  [3:0] SEL,
  output [31:0] out_18
);

  wire [31:0] mux2_1_out_7, mux2_2_out_7, mux2_3_out_7, mux2_4_out_7;

  MUX2 mux2_1 (
    .in_1(L_15_2003d26e), .in_2(L_14_3596d129), .in_3(L_13_2a07598d), .in_4(L_12_c835480d), .in_5(SEL[0]),
    .in_6(SEL[1]), .out_7(mux2_1_out_7));
  MUX2 mux2_2 (
    .in_1(L_11_84717e35), .in_2(L_10_ec759479), .in_3(L_9_c7a5b8e9), .in_4(L_8_b104f76e), .in_5(SEL[0]),
    .in_6(SEL[1]), .out_7(mux2_2_out_7));
  MUX2 mux2_3 (
    .in_1(L_7_fb0cd3a0), .in_2(L_6_f67286b0), .in_3(L_5_5f174e58), .in_4(L_4_179404d2), .in_5(SEL[0]),
    .in_6(SEL[1]), .out_7(mux2_3_out_7));
  MUX2 mux2_4 (
    .in_1(L_3_891e2c2d), .in_2(L_2_2b1fdd56), .in_3(L_1_db51dfe3), .in_4(L_0_d56634bb), .in_5(SEL[0]),
    .in_6(SEL[1]), .out_7(mux2_4_out_7));
  MUX2 mux2_5 (
    .in_1(mux2_1_out_7), .in_2(mux2_2_out_7), .in_3(mux2_3_out_7), .in_4(mux2_4_out_7), .in_5(SEL[2]),
    .in_6(SEL[3]), .out_7(out_18));
endmodule

module two_one_mux (
  input  [31:0] inp_0,
  input  select,
  input  [31:0] inp_1,
  output [31:0] out_4
);

  wire not_1_out;
  wire [31:0] and_1_out, and_2_out, bit_extender_1_out, bit_extender_2_out;

  not not_1 (not_1_out, select);
  assign bit_extender_1_out = {{31{not_1_out}}, not_1_out};  // Bit_Extender bit_extender_1
  assign bit_extender_2_out = {{31{select}}, select};  // Bit_Extender bit_extender_2
  assign and_1_out = inp_0 & bit_extender_1_out;  // AND_Gate and_1, 32 bits wide
  assign and_2_out = bit_extender_2_out & inp_1;  // AND_Gate and_2, 32 bits wide
  assign out_4 = and_1_out | and_2_out;  // OR_Gate or_1, 32 bits wide
endmodule

module MULH (
  input  [31:0] B,
  input  [31:0] A,
  output [31:0] MUL,
  output [31:0] out_4
);

  wire adder_1_cout, xor_1_out;
  wire [31:0] AUS, BUS, L, L_L_9bff1656, L_U_8f1a918a, negator_1_out, negator_2_out, not_1_out, not_2_out, U;

  Negator #(.width(32)) negator_1 (.in(A), .out(negator_1_out));
  Negator #(.width(32)) negator_2 (.in(B), .out(negator_2_out));
  two_one_mux two_one_mux_1 (.inp_0(A), .select(A[31]), .inp_1(negator_1_out), .out_4(AUS));
  two_one_mux two_one_mux_2 (.inp_0(B), .select(B[31]), .inp_1(negator_2_out), .out_4(BUS));
  xor xor_1 (xor_1_out, A[31], B[31]);
  MULHU mulhu_1 (.A(AUS), .B(BUS), .MULH(U), .MULL(L));
  two_one_mux two_one_mux_3 (.inp_0(L), .select(xor_1_out), .inp_1(L_L_9bff1656), .out_4(MUL));
  two_one_mux two_one_mux_4 (.inp_0(U), .select(xor_1_out), .inp_1(L_U_8f1a918a), .out_4(out_4));
  assign not_1_out = ~L;  // NOT_Gate not_1, 32 bits wide
  Adder #(.width(32)) adder_1 (.a(not_1_out), .b(32'h1), .out(L_L_9bff1656), .cout(adder_1_cout));  // open: cin
  assign not_2_out = ~U;  // NOT_Gate not_2, 32 bits wide
  Adder #(.width(32)) adder_2 (.a(not_2_out), .b({32{1'b0}}), .out(L_U_8f1a918a), .cin(adder_1_cout));  // open: cout

  // Other names for the same wires on the sheet: AIN[31:0] = A; AS = A[31]; BIN[31:0] = B; BS = B[31]
endmodule

module mulinbuilt (
  input  [31:0] B,
  input  [31:0] A,
  output [31:0] MUL,
  output [31:0] MULH
);

  Multiplier #(.width(32)) multiplier_1 (.a(A), .b(B), .out(MUL), .cout(MULH));  // open: cin

  // Other names for the same wires on the sheet: AIN[31:0] = A; BIN[31:0] = B
endmodule

module SUM (
  input  [31:0] A,
  input  [31:0] B,
  output [31:0] RESULT,
  output COUT
);

  wire xnor_1_out, xor_1_out;
  wire [31:0] adder_1_out, bit_extender_1_out, bit_extender_2_out;

  assign bit_extender_1_out = {{1{A[31]}}, A[30:0]};  // Bit_Extender bit_extender_1
  assign bit_extender_2_out = {{1{B[31]}}, B[30:0]};  // Bit_Extender bit_extender_2
  xnor xnor_1 (xnor_1_out, A[31], B[31]);
  Adder #(.width(32)) adder_1 (.a(bit_extender_1_out), .b(bit_extender_2_out), .out(adder_1_out));  // open: cin, cout
  xor xor_1 (xor_1_out, adder_1_out[31], A[31]);
  assign RESULT = {{1{adder_1_out[31]}}, adder_1_out[30:0]};  // Bit_Extender bit_extender_3
  and and_1 (COUT, xnor_1_out, xor_1_out);
endmodule

module register_file (
  input  [4:0] Write_Register,
  input  [4:0] Read_Register_1,
  input  [4:0] Read_Register_2,
  input  [31:0] Write_Data,
  input  RegWEn,
  input  clk,
  output [31:0] Read_Data_1,
  output [31:0] Read_Data_2
);

  wire and_1_out, and_2_out, and_3_out, and_4_out, and_5_out, and_6_out, and_7_out, and_8_out, and_9_out,
       decoder_1_out0, decoder_1_out1, decoder_1_out2, decoder_1_out5, decoder_1_out6, decoder_1_out7,
       decoder_1_out8, decoder_1_out9, decoder_1_out10;
  wire [31:0] undriven, x0_q, x1_q, x5_q, x6_q, x7_q, x8_q, x9_q, x10_q;

  Decoder #(.enable("false"), .select(4)) decoder_1 (
    .out0(decoder_1_out0), .out1(decoder_1_out1), .out2(decoder_1_out2), .out5(decoder_1_out5),
    .out6(decoder_1_out6), .out7(decoder_1_out7), .out8(decoder_1_out8), .out9(decoder_1_out9),
    .out10(decoder_1_out10), .sel(Write_Register[3:0]));  // open: out3, out4, out11, out12, out13, out14, out15
  and and_1 (and_1_out, RegWEn, decoder_1_out0);
  and and_2 (and_2_out, RegWEn, decoder_1_out1);
  and and_3 (and_3_out, RegWEn, decoder_1_out10);
  and and_4 (and_4_out, RegWEn, decoder_1_out2);
  and and_5 (and_5_out, RegWEn, decoder_1_out5);
  and and_6 (and_6_out, RegWEn, decoder_1_out6);
  and and_7 (and_7_out, RegWEn, decoder_1_out7);
  and and_8 (and_8_out, RegWEn, decoder_1_out8);
  and and_9 (and_9_out, RegWEn, decoder_1_out9);
  Register #(.width(32)) x0 (.D({32{1'b0}}), .en(and_1_out), .clk(clk), .Q(x0_q));  // open: clr
  Register #(.width(32)) x1 (.D(Write_Data), .en(and_2_out), .clk(clk), .Q(x1_q));  // open: clr
  Register #(.width(32)) x2 (.D(Write_Data), .en(and_4_out), .clk(clk));  // open: Q, clr
  Register #(.width(32)) x5 (.D(Write_Data), .en(and_5_out), .clk(clk), .Q(x5_q));  // open: clr
  Register #(.width(32)) x6 (.D(Write_Data), .en(and_6_out), .clk(clk), .Q(x6_q));  // open: clr
  Register #(.width(32)) x7 (.D(Write_Data), .en(and_7_out), .clk(clk), .Q(x7_q));  // open: clr
  Register #(.width(32)) x8 (.D(Write_Data), .en(and_8_out), .clk(clk), .Q(x8_q));  // open: clr
  Register #(.width(32)) x9 (.D(Write_Data), .en(and_9_out), .clk(clk), .Q(x9_q));  // open: clr
  Register #(.width(32)) x10 (.D(Write_Data), .en(and_3_out), .clk(clk), .Q(x10_q));  // open: clr
  Multiplexer #(.select(4), .width(32)) multiplexer_1 (
    .in0(x0_q), .in1(x1_q), .in2(undriven), .in5(x5_q), .in6(x6_q), .in7(x7_q), .in8(x8_q), .in9(x9_q),
    .in10(x10_q), .out(Read_Data_1), .sel(Read_Register_1[3:0]));  // open: in3, in4, in11, in12, in13, in14, in15
  Multiplexer #(.select(4), .width(32)) multiplexer_2 (
    .in0(x0_q), .in1(x1_q), .in2(undriven), .in5(x5_q), .in6(x6_q), .in7(x7_q), .in8(x8_q), .in9(x9_q),
    .in10(x10_q), .out(Read_Data_2), .sel(Read_Register_2[3:0]));  // open: in3, in4, in11, in12, in13, in14, in15

  // Other names for the same wires on the sheet: WRen = RegWEn
endmodule

// ALU
module single_cycle (
  input  in_1
);

  wire clk, decoder_1_alusrc, mem_read, mem_write, Overflow, PCsel, write, Zero;
  wire [3:0] ALUSel;
  wire [4:0] rd, rs1, rs2;
  wire [7:0] Register_File_read_data_2, Register_File_read_data_2_2, Register_File_read_data_2_3,
       Register_File_read_data_2_4;
  wire [23:0] adder_1_out, adder_2_out, bit_extender_1_out, mem_address, multiplexer_1_out,
       multiplexer_2_out, pc;
  wire [31:0] imm, instr, mem_data, multiplexer_4_out, Op1, Op2, Res;

  Clock clock_1 (.out(clk));
  Register #(.width(24)) u_PC (.D(multiplexer_1_out), .en(1'b1), .clk(clk), .Q(pc), .clr(in_1));
  // Probe on pc
  Multiplexer #(.width(24)) multiplexer_1 (
    .in0(adder_1_out), .in1(multiplexer_2_out), .out(multiplexer_1_out), .sel(PCsel));
  Adder #(.width(24)) adder_1 (.a(24'h4), .b(pc), .out(adder_1_out), .cin(1'b0));  // open: cout
  // RAM #(.addrWidth(24), .enables("line"), .line("quad")) Instruction_memory: pin names not known; wires that end beside it: pc, 1'b0, 1'b1, clk
  // Probe on instr
  decoder decoder_1 (
    .Instruction(instr), .rd(rd), .rs1(rs1), .rs2(rs2), .imm(imm), .write(write), .ALUop(ALUSel),
    .ALUsrc(decoder_1_alusrc), .PCsel(PCsel), .mem_write(mem_write), .reg_write(mem_read),
    .mem_read_30c2a223(mem_read));
  Bit_Extender #(.in_width(32), .out_width(24)) bit_extender_1 (.in(imm), .out(bit_extender_1_out));
  Adder #(.width(24)) adder_2 (.a(pc), .b(bit_extender_1_out), .out(adder_2_out));  // open: cin, cout
  register_file Register_File (
    .Write_Register(rd), .Read_Register_1(rs1), .Read_Register_2(rs2), .Write_Data(multiplexer_4_out),
    .RegWEn(write), .clk(clk), .Read_Data_1(Op1),
    .Read_Data_2({Register_File_read_data_2_4, Register_File_read_data_2_3, Register_File_read_data_2_2, Register_File_read_data_2}));
  Multiplexer #(.width(24)) multiplexer_2 (.in0(adder_1_out), .in1(adder_2_out), .out(multiplexer_2_out), .sel(Zero));
  Multiplexer #(.width(32)) multiplexer_3 (
    .in0(imm),
    .in1({Register_File_read_data_2_4, Register_File_read_data_2_3, Register_File_read_data_2_2, Register_File_read_data_2}),
    .out(Op2), .sel(decoder_1_alusrc));
  // Probe on Op1
  // Probe on Op2
  // Probe on Res
  main ALU (.ALUSel(ALUSel), .A(Op1), .B(Op2), .OverFlow(Overflow), .Zero(Zero), .Result(Res));
  Multiplexer #(.width(32)) multiplexer_4 (.in0(Res), .in1(mem_data), .out(multiplexer_4_out), .sel(mem_read));
  Bit_Extender #(.in_width(32), .out_width(24)) bit_extender_2 (.in(Res), .out(mem_address));
  // RAM #(.addrWidth(24), .enables("line"), .line("quad"), .\type ("nonvolatile")) ram_1: pin names not known; wires that end beside it: mem_address, mem_write, 1'b1, clk, mem_data[7:0], mem_data[15:8], mem_data[23:16], mem_data[31:24]

  // Other names for the same wires on the sheet: reg_write = mem_read; reset = in_1
endmodule

module decoder (
  input  [31:0] Instruction,
  output [4:0] rd,
  output [4:0] rs1,
  output [4:0] rs2,
  output [31:0] imm,
  output write,
  output [3:0] ALUop,
  output ALUsrc,
  output PCsel,
  output mem_write,
  output reg_write,
  output mem_read_30c2a223
);

  wire and_1_out, and_2_out, I_out, LS, not_1_out, not_2_out, not_3_out, not_4_out, not_5_out, not_6_out,
       not_7_out, not_8_out, not_9_out, not_10_out, not_11_out, not_12_out, not_13_out, not_14_out,
       not_15_out, not_16_out, not_17_out, not_18_out, not_19_out, not_20_out, not_21_out, not_22_out,
       or_1_out, or_2_out, R;
  wire [11:0] multiplexer_1_out;
  wire [12:0] bit_extender_1_out, multiplexer_2_out;

  or or_1 (or_1_out, and_1_out, PCsel);
  and and_1 (and_1_out, R, Instruction[30]);
  not not_1 (not_1_out, Instruction[13]);
  not not_2 (not_2_out, Instruction[12]);
  not not_3 (not_3_out, Instruction[14]);
  not not_4 (not_4_out, Instruction[6]);
  not not_5 (not_5_out, Instruction[3]);
  not not_6 (not_6_out, Instruction[2]);
  and u_R (R, not_4_out, Instruction[5], Instruction[4], not_5_out, not_6_out, Instruction[1], Instruction[0]);
  and and_2 (and_2_out, not_1_out, not_2_out, not_3_out, or_1_out);
  or or_2 (or_2_out, and_2_out, Instruction[14]);
  not not_7 (not_7_out, Instruction[6]);
  not not_8 (not_8_out, Instruction[5]);
  not not_9 (not_9_out, Instruction[3]);
  not not_10 (not_10_out, Instruction[2]);
  and I (I_out, not_7_out, not_8_out, Instruction[4], not_9_out, not_10_out, Instruction[1], Instruction[0]);
  and and_3 (ALUop[3], and_2_out, LS);
  and and_4 (ALUop[2], or_2_out, LS);
  and and_5 (ALUop[1], Instruction[13], LS);
  and and_6 (ALUop[0], Instruction[12], LS);
  not not_11 (not_11_out, Instruction[4]);
  not not_12 (not_12_out, Instruction[3]);
  not not_13 (not_13_out, Instruction[2]);
  and SB (PCsel, Instruction[6], Instruction[5], not_11_out, not_12_out, not_13_out, Instruction[1], Instruction[0]);
  xnor xnor_1 (LS, mem_write, mem_read_30c2a223);
  not not_14 (not_14_out, Instruction[6]);
  not not_15 (not_15_out, Instruction[5]);
  not not_16 (not_16_out, Instruction[4]);
  not not_17 (not_17_out, Instruction[3]);
  not not_18 (not_18_out, Instruction[2]);
  and L (mem_read_30c2a223, not_14_out, not_15_out, not_16_out, not_17_out, not_18_out, Instruction[1], Instruction[0]);
  not not_19 (not_19_out, Instruction[6]);
  not not_20 (not_20_out, Instruction[4]);
  not not_21 (not_21_out, Instruction[3]);
  not not_22 (not_22_out, Instruction[2]);
  and S (mem_write, not_19_out, Instruction[5], not_20_out, not_21_out, not_22_out, Instruction[1], Instruction[0]);
  or or_3 (write, I_out, R, mem_read_30c2a223, 1'b0);
  or or_4 (ALUsrc, PCsel, R);
  Multiplexer #(.width(12)) multiplexer_1 (
    .in0(Instruction[31:20]), .in1({Instruction[31:25], Instruction[11:7]}), .out(multiplexer_1_out),
    .sel(mem_write));
  assign bit_extender_1_out = {{1{multiplexer_1_out[11]}}, multiplexer_1_out};  // Bit_Extender bit_extender_1
  Multiplexer #(.width(13)) multiplexer_2 (
    .in0(bit_extender_1_out),
    .in1({Instruction[31], Instruction[7], Instruction[30:25], Instruction[11:8], 1'b0}),
    .out(multiplexer_2_out), .sel(PCsel));
  assign imm = {{19{multiplexer_2_out[12]}}, multiplexer_2_out};  // Bit_Extender bit_extender_2

  assign rd = Instruction[11:7];
  assign reg_write = mem_read_30c2a223;
  assign rs1 = Instruction[19:15];
  assign rs2 = Instruction[24:20];

  // Other names for the same wires on the sheet: b_immed[12:1] = {Instruction[31], Instruction[7], Instruction[30:25], Instruction[11:8]};
  //   funct7[6:0] = Instruction[31:25]; opcode[6:0] = Instruction[6:0]; funct3[2:0] = Instruction[14:12];
  //   L = mem_read_30c2a223; MEM_read = mem_read_30c2a223; S = mem_write; SB = PCsel
endmodule

module SLTU (
  input  [31:0] A,
  input  [31:0] B,
  output [31:0] Out
);

  wire comparator_1_lt;

  Comparator #(.mode("unsigned"), .width(32)) comparator_1 (.a(A), .b(B), .lt(comparator_1_lt));  // open: gt, eq
  assign Out = {{31{comparator_1_lt}}, comparator_1_lt};  // Bit_Extender bit_extender_1
endmodule

module memtest (
);

  RAM #(.addrWidth(24)) ram_1 ();  // open: addr, we, oe, clk, din, dout
  ROM rom_1 ();  // open: addr, data
endmodule
